# Fritzing sketch listwa1 (saved by Fritzing 0.9.3b)
breadboards: 1

parts:
  WeMos_D1_Mini1 = WeMos D1 Mini
  DHT11 = Humidity and Temperature Sensor RHT03
  Part2 = 4 channel SSR

nets:
  5V: WeMos_D1_Mini1.5V, DHT11.Vcc, Part2.DC+
  N1: WeMos_D1_Mini1.D0, DHT11.Data-signal
  N2: WeMos_D1_Mini1.D2, Part2.CH1
  N3: WeMos_D1_Mini1.D5, Part2.CH4
  N4: WeMos_D1_Mini1.D6, Part2.CH2
  N5: WeMos_D1_Mini1.D7, Part2.CH3
  N6: WeMos_D1_Mini1.G, DHT11.GND_2, Part2.DC-

notes:
  4 channel SSR relay
  connectors:
  DC+
  DC-
  CH1
  CH2
  CH3
  CH4
